# Fritzing sketch schema (saved by Fritzing 1.0.5)
breadboards: 1
perfboards: 2

parts:
  Mod1 = Raspberry Pi Pico W
  MIC1 = Microphone
  S1 = Pushbutton [package="[THT]"]
  S2 = Pushbutton [package="[THT]"]
  S3 = Pushbutton [package="[THT]"]
  R1 = Resistor [tolerance=±2% resistance=38 package=THT]

nets:
  N1: Mod1.pin_3, Mod1.pin_8, Mod1.pin_13, Mod1.pin_18, Mod1.pin_23, Mod1.pin_28, Mod1.pin_33, Mod1.pin_38, MIC1.pin1, S1.Pin_3, S1.Pin_4, S2.Pin_3, S2.Pin_4, S3.Pin_3, S3.Pin_4
  N2: Mod1.pin_16, R1.Pin_1
  N3: Mod1.pin_17, S3.Pin_1, S3.Pin_2
  N4: Mod1.pin_19, S1.Pin_1, S1.Pin_2
  N5: Mod1.pin_20, S2.Pin_1, S2.Pin_2
  N6: MIC1.pin2, R1.Pin_0

notes:
  Joystick
  GND
  Motor vibrații
  LCD
  VCC
  VRx
  VRy
  SW
  A0/DC
  CS
  SCK
  LED
  RESET
  SDA

custom parts:
  Raspberry Pi Pico W: Raspberry Pi Pico W. Based around the RP2040 microcontroller the Pico W is a low cost microcontroller device bringing Raspberry Pi quality, cost, and easy of use to the microcontroller space. The areas marked KEEPOUT in pcb silkscreen should not have traces running through them to avoid shorts on a soldered in module!
